# Fritzing sketch Growbox controller (saved by Fritzing 0.9.3b)
breadboards: 1

parts:
  Part1 = Arduino Uno (Rev3) - ICSP
  U1 = ESP8266 WiFi Module [part_number=ESP8266]
  U2 = 2-Channel 5v Relay Shield [package=relay-2ch5v10a]
  R1 = Resistor [tolerance=±5% resistance=330 package="2010 [SMD]"]
  R2 = Resistor [tolerance=±5% resistance=3.3k package="2010 [SMD]"]
  R3 = Resistor [tolerance=±5% resistance=3.3k package="2010 [SMD]"]
  R4 = Resistor [tolerance=±5% resistance=3.3k package="2010 [SMD]"]
  R5 = Resistor [tolerance=±5% resistance=3.3k package="2010 [SMD]"]
  R6 = Resistor [tolerance=±5% resistance=3.3k package="2010 [SMD]"]
  U3 = V_REG_LD1117VXX [package=78xxl]
  C1 = Electrolytic Capacitor [capacitance=10μF package="0605 [SMD, electrolytic]"]
  C2 = Capacitor [package=cap-pth-small2]
  DHT1 = DHT22 Humidity and Temperature Sensor
  D1 = Schottky Diode [part_number=1N5819 package="Melf DO-213 AB [SMD]"]
  R7 = Resistor [tolerance=±5% resistance=10k package="2010 [SMD]"]

nets:
  5V: Part1.5V, U2.VCC, U3.IN, C2.2, DHT1.VDD, R7.Pin_1
  GND: Part1.GND, U1.GND, U2.GND, U3.GND, C1.-, C2.1, DHT1.GND
  N1: Part1.D0/RX, R1.Pin_0
  N2: Part1.D1/TX, D1.cathode
  N3: Part1.D2, U2.IN1
  N4: Part1.D3_PWM, U2.IN2
  N5: Part1.D4, DHT1.DATA, R7.Pin_0
  N6: U1.RXD, R4.Pin_0, D1.anode
  N7: U1.VCC, R2.Pin_1, R3.Pin_1, R4.Pin_1, R5.Pin_1, R6.Pin_1, U3.OUT, C1.+
  N8: U1.GPIO_0, R3.Pin_0
  N9: U1.RST, R6.Pin_0
  N10: U1.GPIO_2, R2.Pin_0
  N11: U1.CH_PD, R5.Pin_0
  N12: U1.TXD, R1.Pin_1

custom parts:
  ESP8266 WiFi Module: Generic WiFi Module based on the ESP8266 with onboard PCB antenna and UART communications
  2-Channel 5v Relay Shield: 2 Channel 5v Relay Shield w. 2x SPD-06VDC-SD-C
